# Fritzing sketch greenhouse (saved by Fritzing 0.9.4)
breadboards: 1

parts:
  VCC1 = 4 x AAA Battery Mount
  Power_plug1 = Power plug
  CONN1 = USB connector [package=THT]
  SP1 = SPEAKER [package=pcb_mount_speaker]
  WeMos_D1_Mini_Relay_Shield_V1 = WeMos D1 Mini Relay Shield V2
  M1 = DC Motor
  U1 = Ambient Light Sensor [package=temt6000-sen]
  J1 = STM32 Nucleo boards

nets:
  N1: VCC1.-, SP1.+, WeMos_D1_Mini_Relay_Shield_V1.G, U1.C1, J1.GND#1149
  N2: VCC1.+, WeMos_D1_Mini_Relay_Shield_V1.5V, J1.PA15
  N3: Power_plug1.VCC, M1.pin_1
  N4: CONN1.GND, J1.GND#880
  N5: SP1.-, J1.PH0
  N6: WeMos_D1_Mini_Relay_Shield_V1.D4, J1.PB1
  N7: U1.E1, J1.PC15
