# Fritzing sketch greenhouse2 (saved by Fritzing 0.9.4)
breadboards: 2

parts:
  Power_plug1 = Power plug
  CONN1 = USB connector [package=THT]
  SP1 = SPEAKER [package=pcb_mount_speaker]
  WeMos_D1_Mini_Relay_Shield_V1 = WeMos D1 Mini Relay Shield V2
  M1 = DC Motor
  U1 = Ambient Light Sensor [package=temt6000-sen]
  J1 = STM32 Nucleo boards
  U2 = Luxeon LED [package=luxeon]
  WeMos_D1_Mini_Relay_Shield_V2 = WeMos D1 Mini Relay Shield V2
  U3 = LIPO-2000mAh [package=lipo-2000]
  U4 = _h3_MPL115A1 (SPI) and MPL115A2 (I2C) Miniature Digital Barometer__h3_ [package=lga8]
  Part1 = Soil Moisture Sensor

nets:
  N1: Power_plug1.GND, U2.A
  N2: Power_plug1.VCC, M1.pin_1
  5V: CONN1.5V, J1.5V
  N3: CONN1.d-, J1.TX
  N4: CONN1.d+, J1.RX
  N5: CONN1.GND, CONN1.chassis5, CONN1.chassis6, J1.GND#880
  GND: SP1.+, WeMos_D1_Mini_Relay_Shield_V1.G, U1.C1, J1.GND#1149, WeMos_D1_Mini_Relay_Shield_V2.G, U3.-, U4.GND, Part1.GND
  N6: SP1.-, J1.PH0
  5V_2: WeMos_D1_Mini_Relay_Shield_V1.5V, J1.PB13, J1.PA15, WeMos_D1_Mini_Relay_Shield_V2.5V, U3.+, U4.VDD, Part1.VCC
  N7: WeMos_D1_Mini_Relay_Shield_V1.D4, J1.PB1
  N8: U1.E1, J1.PC15
  N9: J1.PB15, WeMos_D1_Mini_Relay_Shield_V2.D4
  N10: J1.PH1, Part1.SIG
  N11: J1.VLCD, U4.SCLK
